# Fritzing sketch Count_Down_Launcher (saved by Fritzing 0.9.2b)

parts:
  Part1 = Arduino Uno (Rev3)
  R1 = Resistor [tolerance=±5% resistance=10k package=THT]
  S3 = Relay [part_number=RELAY package=THT]
  M1 = DC Motor
  Vcc = Battery
  S2 = Momentary Switch [package=ksa_sealed_tac_switch]
  S1 = SWITCH_SPDT [package=kps-1290]
  R2 = Resistor [tolerance=±5% resistance=100 package=THT]  # not connected
  LED1 = LED - 5mm [color="Red (633nm)" package="5 mm [THT]"]  # not connected
  LED2 = LED - 5mm [color="Green (565nm)" package="5 mm [THT]"]  # not connected

nets:
  N1: Part1.GND, R1.Pin_1, S3.COIL1
  N2: Part1.D2, S3.COIL2
  N3: Part1.D3_PWM, R1.Pin_0, S2.1
  N4: Part1.3V3, S2.3
  N5: S3.A, S1.O
  N6: S3.B, M1.pin_2
  N7: M1.pin_1, Vcc.+
  N8: Vcc.-, S1.P
